// Logisim project processor.circ as structural Verilog: 1 circuit, main circuit main
module main (
  input  in_1,
  input  in_2,
  input  in_3
);

  wire clock_1_out, comparator_1_eq, comparator_2_eq, comparator_3_eq, comparator_4_eq, main_1_p8;
  wire [4:0] main_1_p1, main_1_p2, main_1_p3, multiplexer_1_out, multiplexer_3_out, multiplexer_4_out,
       multiplexer_6_out, multiplexer_7_out, multiplexer_8_out, rom_1_data_2, rom_1_data_3, rom_1_data_4;
  wire [6:0] rom_1_data;
  wire [9:0] bit_extender_3_out, main_2_p3, multiplexer_13_out, multiplexer_14_out, multiplexer_15_out,
       rom_1_data_5;
  wire [23:0] adder_1_out, PC_q;
  wire [31:0] bit_extender_1_out, bit_extender_2_out, bit_extender_4_out, main_1_p7, main_1_p9, main_2_p2,
       main_2_p5, multiplexer_10_out, multiplexer_11_out, multiplexer_18_out, ram_1_data;

  Clock clock_1 (.out(clock_1_out));
  Register #(.width(24)) PC (.D(adder_1_out), .en(in_1), .Q(PC_q), .clk(clock_1_out), .clr(in_2));
  Adder #(.width(24)) adder_1 (.a(24'h4), .b(PC_q), .out(adder_1_out));  // open: cin, cout
  // regfile_main main_1: pin names not known; wires that end beside it: main_1_p1, main_1_p2, main_1_p3, clock_1_out, in_1, in_3, main_1_p7, main_1_p8, main_1_p9
  ROM #(.addrWidth(10), .dataWidth(32)) rom_1 (
    .addr(PC_q[11:2]),
    .data({rom_1_data_5[9:3], rom_1_data_4, rom_1_data_3, rom_1_data_5[2:0], rom_1_data_2, rom_1_data}));  // open: sel
  Comparator #(.width(7), .mode("unsigned")) comparator_1 (
    .a(rom_1_data), .b(7'b0110011), .eq(comparator_1_eq));  // open: gt, lt
  Comparator #(.width(7), .mode("unsigned")) comparator_2 (
    .a(rom_1_data), .b(7'b0010011), .eq(comparator_2_eq));  // open: gt, lt
  Comparator #(.width(7), .mode("unsigned")) comparator_3 (
    .a(rom_1_data), .b(7'b0000011), .eq(comparator_3_eq));  // open: gt, lt
  Comparator #(.width(7), .mode("unsigned")) comparator_4 (
    .a(rom_1_data), .b(7'b0100011), .eq(comparator_4_eq));  // open: gt, lt
  // finalALu_main main_2: pin names not known; wires that end beside it: main_1_p8, main_2_p2, main_2_p3, comparator_2_eq, main_2_p5
  Multiplexer #(.width(5)) multiplexer_1 (
    .in0({5{1'b0}}), .in1(rom_1_data_4), .out(multiplexer_1_out), .sel(comparator_1_eq));  // open: en
  Multiplexer #(.width(5)) multiplexer_2 (
    .in0(multiplexer_1_out), .in1(rom_1_data_4), .out(main_1_p2), .sel(comparator_4_eq));  // open: en
  Multiplexer #(.width(5)) multiplexer_3 (
    .in0({5{1'b0}}), .in1(rom_1_data_2), .out(multiplexer_3_out), .sel(comparator_1_eq));  // open: en
  Multiplexer #(.width(5)) multiplexer_4 (
    .in0(multiplexer_3_out), .in1(rom_1_data_2), .out(multiplexer_4_out), .sel(comparator_2_eq));  // open: en
  Multiplexer #(.width(5)) multiplexer_5 (
    .in0(multiplexer_4_out), .in1(rom_1_data_2), .out(main_1_p3), .sel(comparator_3_eq));  // open: en
  Multiplexer #(.width(5)) multiplexer_6 (
    .in0({5{1'b0}}), .in1(rom_1_data_3), .out(multiplexer_6_out), .sel(comparator_1_eq));  // open: en
  Multiplexer #(.width(5)) multiplexer_7 (
    .in0(multiplexer_6_out), .in1(rom_1_data_3), .out(multiplexer_7_out), .sel(comparator_2_eq));  // open: en
  Multiplexer #(.width(5)) multiplexer_8 (
    .in0(multiplexer_7_out), .in1(rom_1_data_3), .out(multiplexer_8_out), .sel(comparator_3_eq));  // open: en
  Multiplexer #(.width(5)) multiplexer_9 (
    .in0(multiplexer_8_out), .in1(rom_1_data_3), .out(main_1_p1), .sel(comparator_4_eq));  // open: en
  Multiplexer #(.width(32)) multiplexer_10 (
    .in0(main_1_p9), .in1(bit_extender_1_out), .out(multiplexer_10_out), .sel(comparator_2_eq));  // open: en
  Multiplexer #(.width(32)) multiplexer_11 (
    .in0(multiplexer_10_out), .in1(bit_extender_2_out), .out(multiplexer_11_out), .sel(comparator_3_eq));  // open: en
  Multiplexer #(.width(32)) multiplexer_12 (
    .in0(multiplexer_11_out), .in1(bit_extender_4_out), .out(main_2_p2), .sel(comparator_4_eq));  // open: en
  RAM #(.addrWidth(10), .dataWidth(32), .bus("separate")) ram_1 (
    .addr(main_2_p5[9:0]), .din(multiplexer_18_out), .data(ram_1_data), .str(comparator_4_eq),
    .clk(clock_1_out), .ld(comparator_3_eq));  // open: sel, clr
  assign bit_extender_1_out = {{20{rom_1_data_5[9]}}, {rom_1_data_5[9:3], rom_1_data_4}};  // Bit_Extender bit_extender_1
  Multiplexer #(.width(10)) multiplexer_13 (
    .in0({10{1'b0}}), .in1(rom_1_data_5), .out(multiplexer_13_out), .sel(comparator_1_eq));  // open: en
  Multiplexer #(.width(10)) multiplexer_14 (
    .in0(multiplexer_13_out), .in1(rom_1_data_5), .out(multiplexer_14_out), .sel(comparator_2_eq));  // open: en
  Multiplexer #(.width(10)) multiplexer_15 (
    .in0(multiplexer_14_out), .in1({10{1'b0}}), .out(multiplexer_15_out), .sel(comparator_3_eq));  // open: en
  Multiplexer #(.width(10)) multiplexer_16 (
    .in0(multiplexer_15_out), .in1({10{1'b0}}), .out(main_2_p3), .sel(comparator_4_eq));  // open: en
  assign bit_extender_2_out = {{20{rom_1_data_5[9]}}, {rom_1_data_5[9:3], rom_1_data_4}};  // Bit_Extender bit_extender_2
  Multiplexer #(.width(32)) multiplexer_17 (
    .in0(main_2_p5), .in1(ram_1_data), .out(main_1_p7), .sel(comparator_3_eq));  // open: en
  assign bit_extender_3_out = {{7{1'b0}}, rom_1_data_5[2:0]};  // Bit_Extender bit_extender_3
  Multiplexer #(.width(32)) multiplexer_18 (
    .in1(main_1_p9), .out(multiplexer_18_out), .sel(comparator_4_eq));  // open: in0, en
  assign bit_extender_4_out = {{20{1'b0}}, {rom_1_data_5[9:3], rom_1_data_2}};  // Bit_Extender bit_extender_4

  // Notes on the sheet:
  //   PROGRAM COUNTER
  //   ROM
  //   REGISTER FILE
  //   contents of rom_1 (hex, n*v repeats v):
  //   0 200113 500713 e12423 812783 e78533 0 0 a08113 0 0 0 ffd10193 0 0 0 51c193b
  //   checking Op code
  //   R type
  //   I type
  //   L type
  //   S type
  //   DECODER
  //   RISCV SINGLE CYCLE PROCESSOR
  //   R-TYPE/I-TYPE/L-TYPE/S-TYPE
  //   DESIGNED BY: MUHAMMAD NAMEER
  //   19B-071-CS
  //   rd
  //   rs1
  //   rs2
  //   fun3+7
  //   rs2
  //   rd
  //   rs1
  //   rd
  //   fun3
  //   rs1
  //   imm12
  //   (rs2/imm)
  //   busB
  //   func10
  //   immediate
  //   function7+3
  //   dst
  //   width
  //   base
  //   offset
  //   func10
  //   immediate
  //   CONTROLLER
  //   offset
  //   sw
  //   rs1
  //   rs2
endmodule
